// Logisim project ALU.circ as structural Verilog: 2 circuits, main circuit main
module main (
  input  [2:0] ALUOp,
  input  [15:0] A,
  input  [15:0] B,
  input  in_4,
  output [15:0] Result,
  output [15:0] HI,
  output [15:0] LO,
  output GT,
  output Zero,
  output LT
);

  wire [3:0] and_2_out, and_out;
  wire [15:0] adder_1_out, divider_1_out, divider_1_rem, multiplexer_1_out, multiplexer_2_out,
       multiplier_1_cout, multiplier_1_out, NAND_out, OR_out, shifter_1_out, shifter_2_out, subtractor_1_out;

  assign NAND_out = ~(A & B);  // NAND_Gate NAND, 16 bits wide
  assign OR_out = A | B;  // OR_Gate OR, 16 bits wide
  Adder #(.width(16)) adder_1 (.a(A), .b(B), .out(adder_1_out));  // open: cin, cout
  Subtractor #(.width(16)) subtractor_1 (.a(A), .b(B), .out(subtractor_1_out));  // open: bin, bout
  Multiplier #(.width(16)) multiplier_1 (.a(A), .b(B), .out(multiplier_1_out), .cout(multiplier_1_cout));  // open: cin
  Divider #(.width(16)) divider_1 (.a(A), .b(B), .out(divider_1_out), .rem(divider_1_rem));  // open: upper
  assign and_out = B[3:0] & 4'b1111;  // AND_Gate and, 4 bits wide
  assign and_2_out = B[3:0] & 4'b1111;  // AND_Gate and_2, 4 bits wide
  Multiplexer #(.select(3), .width(16)) multiplexer_1 (
    .in4(multiplier_1_out), .in5(divider_1_out), .out(multiplexer_1_out), .sel(ALUOp));  // open: in0, in1, in2, in3, in6, in7, en
  Multiplexer #(.select(3), .width(16)) multiplexer_2 (
    .in4(multiplier_1_cout), .in5(divider_1_rem), .out(multiplexer_2_out), .sel(ALUOp));  // open: in0, in1, in2, in3, in6, in7, en
  Shifter #(.width(16)) shifter_1 (.in(A), .\dist (and_out), .out(shifter_1_out));
  Shifter #(.width(16), .shift("lr")) shifter_2 (.in(A), .\dist (and_2_out), .out(shifter_2_out));
  Multiplexer #(.select(3), .width(16)) multiplexer_3 (
    .in0(NAND_out), .in1(OR_out), .in2(adder_1_out), .in3(subtractor_1_out), .in4({16{1'b0}}),
    .in5({16{1'b0}}), .in6(shifter_1_out), .in7(shifter_2_out), .out(Result), .sel(ALUOp));  // open: en
  Register #(.width(16)) register_1 (.D(multiplexer_1_out), .Q(LO), .clk(in_4));  // open: en, clr
  Register #(.width(16)) register_2 (.D(multiplexer_2_out), .Q(HI), .clk(in_4));  // open: en, clr
  Comparator #(.width(16)) comparator_1 (.a(A), .b({16{1'b0}}), .gt(GT), .eq(Zero), .lt(LT));

  // Other names for the same wires on the sheet: Clock = in_4

  // Notes on the sheet:
  //   Inputs
  //   Result should be 0 for mul and div
  //   what do I need a clock for 
  //   16 bits all accross the board
  //    Don't add/modify/delete any of the input/output pins in this file!
  //   1. Adder 2. Subtractor 3. AND Gate 4. NOR Gate
  //   A - First ALU input
  //   Outputs
  //   Design your ALU in this file
  //   B - Second ALU input
  //   Result - ALU main result
  //   1. NAND (000), 2. OR (001), 3. ADD (010), 4. SUB (011), 5. MUL (100), 6. DIV (101), 7. SLLV (110), 8. SRLV (111) 
  //   ALUOp - The control signal defining the behaviour of the ALU
  //   HI/LO the value of the ALU registers using for mul/div
  //   GT/Zero/LT - Comparison of input A with zero
  //   Mux selects which arithmetic operation through 2 bit selector "Operation"
  //   branch logic
endmodule

module test (
  input  [2:0] in_1,
  input  [15:0] in_2,
  input  [15:0] in_3
);

  wire button_1_out, main_1_gt, main_1_lt, main_1_zero;
  wire [15:0] main_1_hi, main_1_lo, main_1_result;

  main main_1 (
    .ALUOp(in_1), .A(in_2), .B(in_3), .Result(main_1_result), .GT(main_1_gt), .Zero(main_1_zero),
    .LT(main_1_lt), .in_4(button_1_out), .HI(main_1_hi), .LO(main_1_lo));
  Button button_1 (.out(button_1_out));
  // Probe on main_1_result
  // Probe on main_1_hi
  // Probe on main_1_lo
  // Probe on main_1_gt
  // Probe on main_1_zero
  // Probe on main_1_lt

  // Notes on the sheet:
  //   Test your circuit!
endmodule
