// Logisim project RegFile.circ as structural Verilog: 2 circuits, main circuit main
module main (
  input  [15:0] WriteData0,
  input  [2:0] WriteSelect0,
  input  [2:0] ReadSelect0,
  input  [2:0] ReadSelect1,
  input  WE0,
  input  Clock,
  output [15:0] Reg0,
  output [15:0] Reg1,
  output [15:0] Reg2,
  output [15:0] Reg3,
  output [15:0] Reg4,
  output [15:0] Reg5,
  output [15:0] Reg6,
  output [15:0] Reg7,
  output [15:0] ReadData0,
  output [15:0] ReadData1
);

  wire demultiplexer_1_out0, demultiplexer_1_out1, demultiplexer_1_out2, demultiplexer_1_out3,
       demultiplexer_1_out4, demultiplexer_1_out5, demultiplexer_1_out6, demultiplexer_1_out7;
  wire [15:0] demultiplexer_2_out0, demultiplexer_2_out1, demultiplexer_2_out2, demultiplexer_2_out3,
       demultiplexer_2_out4, demultiplexer_2_out5, demultiplexer_2_out6, demultiplexer_2_out7;

  Demultiplexer #(.select(3)) demultiplexer_1 (
    .out0(demultiplexer_1_out0), .out1(demultiplexer_1_out1), .out2(demultiplexer_1_out2),
    .out3(demultiplexer_1_out3), .out4(demultiplexer_1_out4), .out5(demultiplexer_1_out5),
    .out6(demultiplexer_1_out6), .out7(demultiplexer_1_out7), .in(WE0), .sel(WriteSelect0));  // open: en
  Demultiplexer #(.select(3), .width(16)) demultiplexer_2 (
    .out0(demultiplexer_2_out0), .out1(demultiplexer_2_out1), .out2(demultiplexer_2_out2),
    .out3(demultiplexer_2_out3), .out4(demultiplexer_2_out4), .out5(demultiplexer_2_out5),
    .out6(demultiplexer_2_out6), .out7(demultiplexer_2_out7), .in(WriteData0), .sel(WriteSelect0));  // open: en
  Register #(.width(16)) u_Reg0 (
    .D(demultiplexer_2_out0), .en(demultiplexer_1_out0), .Q(Reg0), .clk(Clock));  // open: clr
  Register #(.width(16)) u_Reg1 (
    .D(demultiplexer_2_out1), .en(demultiplexer_1_out1), .Q(Reg1), .clk(Clock));  // open: clr
  Register #(.width(16)) u_Reg2 (
    .D(demultiplexer_2_out2), .en(demultiplexer_1_out2), .Q(Reg2), .clk(Clock));  // open: clr
  Register #(.width(16)) u_Reg3 (
    .D(demultiplexer_2_out3), .en(demultiplexer_1_out3), .Q(Reg3), .clk(Clock));  // open: clr
  Register #(.width(16)) u_Reg4 (
    .D(demultiplexer_2_out4), .en(demultiplexer_1_out4), .Q(Reg4), .clk(Clock));  // open: clr
  Register #(.width(16)) u_Reg5 (
    .D(demultiplexer_2_out5), .en(demultiplexer_1_out5), .Q(Reg5), .clk(Clock));  // open: clr
  Register #(.width(16)) u_Reg6 (
    .D(demultiplexer_2_out6), .en(demultiplexer_1_out6), .Q(Reg6), .clk(Clock));  // open: clr
  Register #(.width(16)) u_Reg7 (
    .D(demultiplexer_2_out7), .en(demultiplexer_1_out7), .Q(Reg7), .clk(Clock));  // open: clr
  Multiplexer #(.select(3), .width(16)) multiplexer_1 (
    .in0(Reg0), .in1(Reg1), .in2(Reg2), .in3(Reg3), .in4(Reg4), .in5(Reg5), .in6(Reg6), .in7(Reg7),
    .out(ReadData0), .sel(ReadSelect0));  // open: en
  Multiplexer #(.select(3), .width(16)) multiplexer_2 (
    .in0(Reg0), .in1(Reg1), .in2(Reg2), .in3(Reg3), .in4(Reg4), .in5(Reg5), .in6(Reg6), .in7(Reg7),
    .out(ReadData1), .sel(ReadSelect1));  // open: en

  // Other names for the same wires on the sheet: WriteEnable0 = WE0

  // Notes on the sheet:
  //   Inputs
  //   Add the registers to this file
  //   WriteSelect0 - Register to write to
  //   ReadSelect0 - First register to read data from
  //   WE0 - Enable writing to 1 register
  //   WriteData0 - The data to be written to register by most instructions
  //   ReadSelect1 - Second register to read data from
  //   ReadData0 - Data being read from first register
  //   ReadData1 - Data being read from second register
  //   Enabling the register to be written to
  //   sending to both readData 1 and Read Data 2
  //   and design the logic to control them
  //   Read 2, Write 1
  //   The data that is being written to a registers
  //    Don't add/modify/delete any of the input/output pins in this file!
  //   I think you want to capture the output but I am not completely sure
  //   Tunnel from Master Clock
  //   Read port 1 select signal, a mux, and a data output
  //   Multiplexers use Select to choose one of many inputs
  //   The data from the reg
  //   Selecting which register should be read from (#2)
endmodule

module test (
  input  [15:0] Write_data_A,
  input  Write_Enable_Port_A,
  input  [2:0] in_3,
  input  [2:0] Select_Read_A,
  input  [2:0] Select_Read_B
);

  wire Clock_out;
  wire [15:0] main_1_readdata0, main_1_readdata1, main_1_reg0, main_1_reg1, main_1_reg2, main_1_reg3,
       main_1_reg4, main_1_reg5, main_1_reg6, main_1_reg7;

  // Probe on main_1_reg1
  // Probe on main_1_reg0
  // Probe on main_1_reg2
  // Probe on main_1_reg3
  Button Clock (.out(Clock_out));
  // Probe on main_1_reg4
  // Probe on main_1_reg5
  // Probe on main_1_reg6
  // Probe on main_1_reg7
  main main_1 (
    .ReadData0(main_1_readdata0), .ReadData1(main_1_readdata1), .Reg0(main_1_reg0), .Reg1(main_1_reg1),
    .Reg2(main_1_reg2), .Reg3(main_1_reg3), .Reg4(main_1_reg4), .Reg5(main_1_reg5), .Reg6(main_1_reg6),
    .Reg7(main_1_reg7), .WriteData0(Write_data_A), .WriteSelect0(in_3), .ReadSelect0(Select_Read_A),
    .ReadSelect1(Select_Read_B), .WE0(Write_Enable_Port_A), .Clock(Clock_out));
  // Probe on main_1_readdata0
  // Probe on main_1_readdata1

  // Notes on the sheet:
  //   Test your circuit!
endmodule
