// Logisim project garbage.circ as structural Verilog: 1 circuit, main circuit main
module main (
  output [15:0] out_1,
  output [15:0] out_2
);

  wire ADD, ADDI, BN, BP, BX, BZ, DIV, GT, halt, I_TYPE, J_IMM, JAL, JR, LT, MUL, OR, put, SLLV;
  wire [3:0] undriven;
  wire [15:0] not_1_p2;
  wire [15:1] xor_2_out, xor_out;

  // NOT_Gate #(.width(16)) not_1: pin names not known; wires that end beside it: {16{1'b0}}, not_1_p2
  assign out_2 = ~(out_1 & {16{1'b0}});  // NAND_Gate nand_1, 16 bits wide
  assign {xor_out, GT} = not_1_p2 ^ out_1;  // XOR_Gate xor, 16 bits wide
  assign {xor_2_out, LT} = {16{1'b0}} ^ out_1;  // XOR_Gate xor_2, 16 bits wide
  Decoder #(.select(4)) decoder_1 (
    .out0(ADD), .out2(DIV), .out3(BP), .out4(BN), .out5(BX), .out6(BZ), .out7(JR), .out8(JAL), .out9(J_IMM),
    .out10(MUL), .out11(put), .out12(OR), .out14(SLLV), .out15(halt), .sel(undriven));  // open: out1, out13, en
  or u_I_TYPE (I_TYPE, ADD, ADDI, DIV, BP, J_IMM, BN, BX, BZ, JAL);

  // Other names for the same wires on the sheet: A[15:0] = out_1; ADDUI = ADD; LI = DIV; LW = BX; MFHI = J_IMM;
  //   MFLO = ADDI; NAND = BN; Zero = out_2[0]; SRLV = BZ; SUB = JAL

  // Notes on the sheet:
  //   branch logic
endmodule
