// Logisim project umips.circ as structural Verilog: 2 circuits, main circuit main
module main (
  output [15:0] Reg0,
  output [15:0] Reg1,
  output [15:0] Reg2,
  output [15:0] Reg3,
  output [15:0] Reg4,
  output [15:0] Reg5,
  output [15:0] Reg6,
  output [15:0] Reg7,
  output [3:0] Output3,
  output [3:0] Output2,
  output [3:0] Output1,
  output [3:0] Output0,
  output halt
);

  wire ALUSrc, bn_out, bp_out, bx_out, bz_out, clock_1_out, decoder_1_out1, decoder_1_out2, decoder_1_out3,
       decoder_1_out4, Jump, main_2_gt, main_2_lt, main_2_zero, MemRead, MemWrite, not_1_p1, not_2_out,
       or_1_out, putEnable, RegWrite, signExt, SubOp, undriven, undriven_2, Useless, Useless_2;
  wire [1:0] JumpOp;
  wire [2:0] ALUOp, branchOp, rs, WriteDataSel;
  wire [7:0] demultiplexer_1_out0, demultiplexer_1_out1, im8, main_1_readdata1, main_1_readdata1_2,
       multiplexer_1_out, multiplexer_2_out, multiplexer_3_out, PC_1, register_1_q;
  wire [15:0] bit_extender_1_out, Hi, Lo, main_2_result, multiplexer_5_out, Put, ram_1_data, UseIm8,
       WriteData;
  wire [15:12] rom_1_data;

  Multiplexer #(.width(8)) multiplexer_1 (.in0(PC_1), .in1(im8), .out(multiplexer_1_out), .sel(or_1_out));  // open: en
  Adder adder_1 (.a(8'h1), .b(register_1_q), .out(PC_1));  // open: cin, cout
  Register register_1 (.D(multiplexer_3_out), .en(not_1_p1), .Q(register_1_q), .clk(clock_1_out));  // open: clr
  // NOT_Gate not_1: pin names not known; wires that end beside it: not_1_p1, halt
  Multiplexer #(.select(2), .width(8)) multiplexer_2 (
    .in1(im8), .in2(Put[7:0]), .in3(im8), .out(multiplexer_2_out), .sel(JumpOp));  // open: in0, en
  // Probe on JumpOp
  Multiplexer #(.width(8)) multiplexer_3 (
    .in0(multiplexer_1_out), .in1(multiplexer_2_out), .out(multiplexer_3_out), .sel(Jump));  // open: en
  ROM #(.dataWidth(16)) rom_1 (.addr(register_1_q), .data({rom_1_data, rs, im8, SubOp}), .sel(1'b1));
  Control CONTROL (
    .SubOp(SubOp), .Opcode(rom_1_data), .halt(halt), .IsJump(Jump), .isBranch(Useless_2), .MemRead(MemRead),
    .MemtoReg(Useless), .ALUOp(ALUOp), .MemWrite(MemWrite), .ALUSrc(ALUSrc), .RegWrite(RegWrite),
    .putEnable(putEnable), .signExt(signExt), .WriteDataSelect(WriteDataSel), .BranchOpcode(branchOp),
    .JumpOpcode(JumpOp));
  Demultiplexer #(.width(8)) demultiplexer_1 (
    .out0(demultiplexer_1_out0), .out1(demultiplexer_1_out1), .in(im8), .sel(signExt));  // open: en
  assign bit_extender_1_out = {{8{demultiplexer_1_out1[7]}}, demultiplexer_1_out1};  // Bit_Extender bit_extender_1
  Multiplexer #(.width(16)) multiplexer_4 (
    .in0({{8{1'b0}}, demultiplexer_1_out0}), .in1(bit_extender_1_out), .out(UseIm8), .sel(signExt));  // open: en
  RegFile_main main_1 (
    .ReadData0(Put), .ReadData1({main_1_readdata1_2, main_1_readdata1}), .Reg0(Reg0), .Reg1(Reg1),
    .Reg2(Reg2), .Reg3(Reg3), .Reg4(Reg4), .Reg5(Reg5), .Reg6(Reg6), .Reg7(Reg7), .WriteData0(WriteData),
    .WriteSelect0(rs), .ReadSelect0(rs), .ReadSelect1(im8[7:5]), .WE0(RegWrite), .Clock(clock_1_out));
  // Probe on UseIm8
  or or_1 (or_1_out, bp_out, bn_out, bx_out, bz_out);
  Clock clock_1 (.out(clock_1_out));
  // Probe on Lo
  // Probe on Hi
  ALU_main main_2 (
    .ALUOp(ALUOp), .A(Put), .B(multiplexer_5_out), .Result(main_2_result), .GT(main_2_gt),
    .Zero(main_2_zero), .LT(main_2_lt), .in_4(clock_1_out), .HI(Hi), .LO(Lo));
  Multiplexer #(.width(16)) multiplexer_5 (
    .in0({main_1_readdata1_2, main_1_readdata1}), .in1(UseIm8), .out(multiplexer_5_out), .sel(ALUSrc));  // open: en
  and bp (bp_out, decoder_1_out1, main_2_gt, undriven);
  and bn (bn_out, undriven, decoder_1_out2, main_2_lt, undriven_2);
  and bx (bx_out, undriven_2, decoder_1_out3, not_2_out);
  and bz (bz_out, decoder_1_out4, main_2_zero);
  not not_2 (not_2_out, main_2_zero);
  // Probe on branchOp
  Decoder #(.select(3)) decoder_1 (
    .out1(decoder_1_out1), .out2(decoder_1_out2), .out3(decoder_1_out3), .out4(decoder_1_out4), .sel(branchOp));  // open: out0, out5, out6, out7, en
  Hex_Digit_Display hex_digit_display_1 (.value(Output3));  // open: dp
  Hex_Digit_Display hex_digit_display_2 (.value(Output2));  // open: dp
  Hex_Digit_Display hex_digit_display_3 (.value(Output1));  // open: dp
  RAM #(.dataWidth(16), .bus("separate")) ram_1 (
    .addr(main_1_readdata1), .din(Put), .data(ram_1_data), .str(MemWrite), .clk(clock_1_out), .ld(MemRead));  // open: sel, clr
  Hex_Digit_Display hex_digit_display_4 (.value(Output0));  // open: dp
  LED HALT_LED (.in(halt));
  LED HALT_LED_2 (.in(halt));
  Multiplexer #(.select(3), .width(16)) multiplexer_6 (
    .in0(main_2_result), .in1(ram_1_data), .in2(Lo), .in3(Hi), .in4(UseIm8), .in5({{8{1'b0}}, PC_1}),
    .out(WriteData), .sel(WriteDataSel));  // open: in6, in7, en
  // Probe on WriteDataSel
  Register #(.width(16)) Puts_reg (
    .D(Put), .en(putEnable), .Q({Output3, Output2, Output1, Output0}), .clk(clock_1_out));  // open: clr

  // Other names for the same wires on the sheet: rsOut[15:0] = Put

  // Notes on the sheet:
  //   PC SECTION
  //   May need to restart Logisim
  //   Instruction Memory - ROM
  //   contents of rom_1 (hex, n*v repeats v):
  //   8a09 2e0b be00 f001 2e19 be00 7a01 2fc5 be00 f001 2fc7 be00 f001
  //   OpCode
  //   Instruction
  //   Rs
  //   Rt
  //   ALUOp enable
  //   If you change them in there, changes will be reflected here!
  //   There circuits are in the other 2 files I gave you... I've imported them to this file
  //   8-bit Immediate
  //   no mux for rd
  //   Zero extend 8 bits 
  //   You must connect Reg0..7 to the top ports of the register file.
  //   youi need to make sure its a good branch, 
  //   RegFile A send to ALU
  //   Immediate or RegFile
  //   ALU Control here if needed
  //   THE CLOCK
  //    Don't add/modify/delete any of the input/output pins in this file!
  //   memory logic here
  //   Data Memory - RAM
  //   Design your CPU in this file
  //   Connect Output3..0 to your LED display.
  //   Output3 is the most significant
  //   LED Hexadecimal display
  //   Include everything here (ALU, RegFile, Control, PC, RAM, ROM, LEDs, Displays, ...)
  //   The data being written to reg
  //   Special case, using data from mul/div
  //   Connect halt to your halt LED
endmodule

module Control (
  input  SubOp,
  input  [3:0] Opcode,
  output halt,
  output IsJump,
  output isBranch,
  output MemRead,
  output MemtoReg,
  output [2:0] ALUOp,
  output MemWrite,
  output ALUSrc,
  output RegWrite,
  output putEnable,
  output signExt,
  output [2:0] WriteDataSelect,
  output [2:0] BranchOpcode,
  output [1:0] JumpOpcode
);

  wire ADD, ADDUI, BN, BP, BX, BZ, decoder_1_out0, decoder_1_out1, decoder_1_out2, decoder_1_out3,
       decoder_1_out4, decoder_1_out5, decoder_1_out6, decoder_1_out7, decoder_1_out8, decoder_1_out9,
       decoder_1_out10, decoder_1_out11, decoder_1_out12, decoder_1_out13, decoder_1_out14, decoder_1_out15,
       demultiplexer_11_out1, DIV, J_IMM, JAL, JR, LI, MFHI, MFLO, MUL, NAND, OR, or_1_out, or_2_out,
       or_3_out, or_4_out, or_5_out, or_6_out, or_7_out, or_8_p4, or_9_p3, or_9_p4, or_11_out, or_12_p2,
       or_12_p3, or_14_out, or_15_out, or_16_out, or_17_out, or_18_out, or_19_out, or_20_out, or_21_p5,
       or_24_out, or_26_out, or_28_out, or_29_out, or_30_out, or_31_p4, or_32_out, or_33_out, or_34_out,
       SLLV, SRLV, SUB, undriven, undriven_2;

  Demultiplexer demultiplexer_1 (.out0(ADD), .out1(ADDUI), .in(decoder_1_out0), .sel(SubOp));  // open: en
  Decoder #(.select(4)) decoder_1 (
    .out0(decoder_1_out0), .out1(decoder_1_out1), .out2(decoder_1_out2), .out3(decoder_1_out3),
    .out4(decoder_1_out4), .out5(decoder_1_out5), .out6(decoder_1_out6), .out7(decoder_1_out7),
    .out8(decoder_1_out8), .out9(decoder_1_out9), .out10(decoder_1_out10), .out11(decoder_1_out11),
    .out12(decoder_1_out12), .out13(decoder_1_out13), .out14(decoder_1_out14), .out15(decoder_1_out15),
    .sel(Opcode));  // open: en
  or or_1 (or_1_out, ADD, SUB);
  or or_2 (or_2_out, NAND, OR);
  or or_3 (or_3_out, ADDUI, signExt);
  or or_4 (or_4_out, SLLV, SRLV);
  or or_5 (or_5_out, MFLO, MFHI);
  or or_6 (or_6_out, MemRead, LI);
  or or_7 (or_7_out, JAL, 1'b0);
  // OR_Gate or_8: pin names not known; wires that end beside it: or_1_out, or_1_out, or_2_out, or_8_p4
  // OR_Gate or_9: pin names not known; wires that end beside it: or_2_out, or_8_p4, or_9_p3, or_9_p4
  or or_10 (or_9_p3, or_3_out, or_4_out);
  or or_11 (or_11_out, or_5_out, or_6_out);
  // OR_Gate or_12: pin names not known; wires that end beside it: or_11_out, or_12_p2, or_12_p3
  or or_13 (or_12_p2, or_7_out, 1'b0);
  Demultiplexer demultiplexer_2 (.out0(MFLO), .out1(signExt), .in(decoder_1_out1), .sel(SubOp));  // open: en
  or or_14 (or_14_out, JAL, JR);
  or or_15 (or_15_out, J_IMM, 1'b0);
  or or_16 (or_16_out, BP, BN);
  or or_17 (or_17_out, BX, BZ);
  or or_18 (or_18_out, ADDUI, signExt, undriven);
  or or_19 (or_19_out, undriven, MemRead, MemWrite);
  or or_20 (or_20_out, LI, 1'b0, 1'b0);
  // OR_Gate or_21: pin names not known; wires that end beside it: 1'b0, 1'b0, 1'b0, LI, or_21_p5, or_20_out
  Demultiplexer demultiplexer_3 (.out0(DIV), .out1(LI), .in(decoder_1_out2), .sel(SubOp));  // open: en
  // OR_Gate or_22: pin names not known; wires that end beside it: JAL, JR, J_IMM, 1'b0, or_14_out, or_14_out, or_15_out, IsJump
  // OR_Gate or_23: pin names not known; wires that end beside it: BP, BN, BX, BZ, or_16_out, or_16_out, or_17_out, isBranch
  or or_24 (or_24_out, or_18_out, or_18_out, or_19_out, or_19_out);
  or or_25 (ALUSrc, or_24_out, or_26_out);
  or or_26 (or_26_out, or_20_out, or_20_out, or_21_p5, or_21_p5);
  or or_27 (RegWrite, or_9_p4, or_12_p3);
  or or_28 (or_28_out, ADD, 1'b0);
  or or_29 (or_29_out, signExt, ADDUI);
  or or_30 (or_30_out, 1'b0, OR);
  // OR_Gate or_31: pin names not known; wires that end beside it: or_28_out, or_29_out, or_29_out, or_31_p4
  Demultiplexer demultiplexer_4 (.out1(BP), .in(decoder_1_out3), .sel(SubOp));  // open: out0, en
  Demultiplexer demultiplexer_5 (.out0(NAND), .out1(BN), .in(decoder_1_out4), .sel(SubOp));  // open: en
  or or_32 (or_32_out, signExt, undriven_2);
  or or_33 (or_33_out, or_32_out, or_32_out, or_34_out, or_34_out);
  or or_34 (or_34_out, undriven_2, ADDUI);
  Priority_Encoder priority_encoder_1 (
    .in0(1'b1), .in1(or_30_out), .in2(or_31_p4), .in3(SUB), .in4(MUL), .in5(DIV), .in6(SLLV), .in7(SRLV),
    .out(ALUOp));  // open: en_in, gs, en_out
  Demultiplexer demultiplexer_6 (.out0(MemRead), .out1(BX), .in(decoder_1_out5), .sel(SubOp));  // open: en
  Priority_Encoder priority_encoder_2 (
    .in0(1'b1), .in1(MemRead), .in2(MFLO), .in3(MFHI), .in4(or_33_out), .in5(JAL), .out(WriteDataSelect));  // open: in6, in7, en_in, gs, en_out
  Priority_Encoder priority_encoder_3 (
    .in0(1'b1), .in1(BP), .in2(BN), .in3(BX), .in4(BZ), .out(BranchOpcode));  // open: in5, in6, in7, en_in, gs, en_out
  Priority_Encoder #(.select(2)) priority_encoder_4 (
    .in0(1'b1), .in1(J_IMM), .in2(JR), .in3(JAL), .out(JumpOpcode));  // open: gs, en_out, en_in
  Demultiplexer demultiplexer_7 (.out0(SRLV), .out1(BZ), .in(decoder_1_out6), .sel(SubOp));  // open: en
  Demultiplexer demultiplexer_8 (.out1(JR), .in(decoder_1_out7), .sel(SubOp));  // open: out0, en
  Demultiplexer demultiplexer_9 (.out0(SUB), .out1(JAL), .in(decoder_1_out8), .sel(SubOp));  // open: en
  Demultiplexer demultiplexer_10 (.out0(MFHI), .out1(J_IMM), .in(decoder_1_out9), .sel(SubOp));  // open: en
  Demultiplexer demultiplexer_11 (
    .out0(MUL), .out1(demultiplexer_11_out1), .in(decoder_1_out10), .sel(SubOp));  // open: en
  Demultiplexer demultiplexer_12 (.out0(putEnable), .in(decoder_1_out11), .sel(SubOp));  // open: out1, en
  Demultiplexer demultiplexer_13 (.out0(OR), .in(decoder_1_out12), .sel(SubOp));  // open: out1, en
  Demultiplexer demultiplexer_14 (.out0(MemWrite), .in(decoder_1_out13), .sel(SubOp));  // open: out1, en
  Demultiplexer demultiplexer_15 (.out0(SLLV), .in(decoder_1_out14), .sel(SubOp));  // open: out1, en
  Demultiplexer demultiplexer_16 (.out1(halt), .in(decoder_1_out15), .sel(SubOp));  // open: out0, en

  assign MemtoReg = MemRead;

  // Other names for the same wires on the sheet: ADDI = signExt; LW = MemRead; put = putEnable; SW = MemWrite

  // Notes on the sheet:
  //   might need to ask about this but moving LI because NAND doesnt work for LI in ALU
  //   Decoder for selecting tunnels based off of opcode
  //   If any are true then a Register is being written to so WriteEnable = 1
  //   CONTROL - CPU - BRANDON HOOVER
  //   An insane amount of OR's
  //   Output 1 Bit Control Signals
  //   DISREGARD 
  //   DISREGARD 
  //   Priority Encoder to send the right value to to ALUOp which ALU takes and executes
  //   Is this the ALU Control, gives you the Opcode for the ALU
  //   are you branching or jumping
  //   does it involve the ALU
  //   are we working with immediates
  //   WriteDataSelect
  //   BranchPriorityEncoder
  //   JunpPriorityEncoder
  //   NAND will always be triggered
  //   Are we going to read memory, then activate load port on RAM
  //   Are we going to write to memory, then activate store port on RAM
  //   SubOp is the selector which instruction to execute since many instructions share the same OpCode
  //   so does it need to trigger for 0 as well because that would be hard
  //   Selector is X
endmodule
